# Fritzing sketch schematic (saved by Fritzing 0.9.3b)
breadboards: 1

parts:
  Composant1 = Arduino Nano (Rev3.0)
  S1 = Pushbutton [package="[SMD]"]
  Q1 = NPN-Transistor [package="TO92 [THT]"]
  D1 = Rectifier Diode [part_number=1N4001 package="300 mil [THT]"]
  VCC1 = Battery block 9V
  S2 = Pushbutton [package="[SMD]"]
  R1 = Resistor [tolerance=±5% resistance=220 package="0603 [SMD]"]
  R2 = Resistor [tolerance=±5% resistance=220 package="0603 [SMD]"]
  SP1 = SPEAKER [package=pcb_mount_speaker]
  SP2 = SPEAKER [package=pcb_mount_speaker]

nets:
  N1: Composant1.GND, S1.Pin_1, S1.Pin_2, VCC1.-, R1.Pin_0, SP1.+, SP2.+
  N2: Composant1.D2, S1.Pin_3, S1.Pin_4
  N3: Composant1.D3, SP1.-
  N4: Composant1.D5, SP2.-
  N5: Composant1.D6, Q1.B, S2.Pin_3, S2.Pin_4
  N6: Composant1.VIN, Q1.C
  N7: Q1.E, D1.cathode
  N8: D1.anode, VCC1.+, R2.Pin_1
  N9: S2.Pin_1, S2.Pin_2, R1.Pin_1, R2.Pin_0

// code stored in the sketch: schematic.ino

